# Fritzing sketch Antenna Amplifier (saved by Fritzing 0.9.2b)
breadboards: 1

parts:
  J1 = Power Jack [package=power_jack_smd]
  R1 = Resistor [tolerance=±20% resistance=27k package="0603 [SMD]"]
  R2 = Resistor [tolerance=±5% resistance=270 package="0603 [SMD]"]
  R3 = Resistor [tolerance=±5% resistance=1k package=THT]
  C1 = Ceramic Capacitor [capacitance=5.6pF voltage=0.1kV package="1206 [SMD, multilayer]"]
  C2 = Ceramic Capacitor [capacitance=5.6pF voltage=0.1kV package="1206 [SMD, multilayer]"]
  C3 = Ceramic Capacitor [capacitance=1nF voltage=10V package="0603 [SMD, multilayer]"]
  C4 = Ceramic Capacitor [capacitance=0.1µF voltage=0.1kV package="1206 [SMD, multilayer]"]
  C5 = Ceramic Capacitor [capacitance=10pF voltage=0.1kV package="1206 [SMD, multilayer]"]
  C6 = Ceramic Capacitor [capacitance=10pF voltage=0.1kV package="1206 [SMD, multilayer]"]
  L1 = Inductor [part_number="4T, 20 SWG 5mm DIA, AIR CORE" package="1206 [SMD]"]
  L2 = Inductor [part_number="3T, 20SWG 5mm DIA, AIR CORE" package="1206 [SMD]"]
  2SC2570 = NPN-Transistor [package="TO92 [THT]"]
  J$1 = SMA Antenna Connector [package=sma-edge]
  J$2 = SMA Antenna Connector [package=sma-edge]
  Part4 = Variable Capacitor [capacitance=100nF max_capacitance=10pF min_capacitance=2pF voltage=35V]
  Part3 = Variable Capacitor [capacitance=100nF max_capacitance=10pF min_capacitance=2pF voltage=35V]

nets:
  N1: J1.PWR, R3.Pin_0, C6.1
  GND: J1.GND, J1.GNDBREAK, C3.0, C6.0, L1.pin_0, L2.pin_1, 2SC2570.E, J$1.GND, J$2.GND, Part4.0, Part3.0
  N2: R1.Pin_0, C2.1, 2SC2570.B
  N3: R1.Pin_1, R2.Pin_0, C4.1, 2SC2570.C
  N4: R2.Pin_1, R3.Pin_1, C3.1
  N5: C1.0, C2.0
  N6: C1.1, J$1.SIGNAL
  N7: C4.0, C5.1, L2.pin_0, Part4.1
  N8: C5.0, J$2.SIGNAL
  N9: L1.pin_1, Part3.1
